# Fritzing sketch Eco_Light (saved by Fritzing 0.8.7b)
breadboards: 1

parts:
  Part1 = Arduino Mega 2560 (Rev3)
  R2 = PHOTOCELL [package=photocell-kit]
  R1 = Resistor [tolerance=±5% resistance=10k package="1206 [SMD]"]
  R1_2 = Resistor [tolerance=±5% resistance=10k package="0805 [SMD]"]
  R3 = Resistor [tolerance=±5% resistance=220 package="0805 [SMD]"]
  LED1 = LEDs [package=led10mm]

nets:
  N1: Part1.GND, R1.Pin_1, R1_2.Pin_1, R3.Pin_1
  N2: Part1.D13_PWM, LED1.A
  N3: Part1.D8_PWM, R2.P$1, R1.Pin_0, R1_2.Pin_0
  N4: Part1.5V, R2.P$2
  N5: R3.Pin_0, LED1.C
