# Fritzing sketch Security_Alarm (saved by Fritzing 0.8.7b)
breadboards: 1

parts:
  Part1 = Arduino Mega 2560 (Rev3)
  J1 = Infrared Proximity Sensor
  LED1 = LEDs [package=led10mm]
  R1 = Resistor [tolerance=±5% resistance=220 package="0805 [SMD]"]

nets:
  GND: Part1.GND, J1.GND, R1.Pin_1
  N1: Part1.D13_PWM, LED1.A
  5V: Part1.5V, J1.Vcc
  N2: Part1.D7_PWM, J1.Vout
  N3: LED1.C, R1.Pin_0
