# Fritzing sketch Temperature_Fan (saved by Fritzing 0.8.7b)
breadboards: 1

parts:
  Part1 = Arduino Mega 2560 (Rev3)
  T1 = TMP36 Temperature Sensor [package="TO92 [THT]"]
  J1 = Basic Servo

nets:
  N1: Part1.A0, T1.Vout
  GND: Part1.GND, T1.GND, J1.gnd
  N2: Part1.D8_PWM, J1.pulse
  5V: Part1.5V, T1.+Vs, J1.vcc
